# Fritzing sketch rbgLed (saved by Fritzing 0.9.2b)
breadboards: 1

parts:
  Nano1 = Arduino Nano v2.3
  R1 = Resistor [tolerance=±5% resistance=220 package=THT]
  R2 = Resistor [tolerance=±5% resistance=220 package=THT]
  R3 = Resistor [tolerance=±5% resistance=220 package=THT]
  LED1 = RGB LED - (4 legs) [package="5 mm [THT]"]

nets:
  N1: Nano1.GND, LED1.common_anode
  N2: Nano1.D3, R1.Pin_0
  N3: Nano1.D5, R3.Pin_0
  N4: Nano1.D6, R2.Pin_0
  N5: R1.Pin_1, LED1.red_cathode
  N6: R2.Pin_1, LED1.green_cathode
  N7: R3.Pin_1, LED1.blue_cathode
